# Fritzing sketch schematic (saved by Fritzing 0.9.2b)
circuit board: 8.46667cm x 5.64444cm

parts:
  U1 = ESP8266 WiFi Module [part_number=ESP8266]
  JP1 = Header 3 [package=jst-3-pth]
  JP2 = Header 3 [package=jst-3-pth]
  JP3 = Header 3 [package=jst-3-pth]
  JP4 = Header 3 [package=jst-3-pth]
  Onderdeel1 = FTDI Basic Programmer

nets:
  N1: U1.IO0, JP2.1
  N2: U1.IO2, U1.T_OUT, JP1.1
  N3: U1.IO4, JP3.1
  N4: U1.IO5, JP4.1
  GND: U1.GND, JP1.3, JP2.3, JP3.3, JP4.3, Onderdeel1.GND
  N5: U1.TX, Onderdeel1.RXI
  N6: U1.RX, Onderdeel1.TXO
  N7: U1.3.3V, JP1.2, JP2.2, JP3.2, JP4.2, Onderdeel1.POWER
